// Logisim project My CPU.circ as structural Verilog
module _16_bit_ALU (
  input  [15:0] A,
  input  [15:0] B,
  input  [1:0] ALU_Op,
  output [15:0] ALU_Out,
  output Zero,
  output Negative
);

  wire and_1_out, or_3_out;
  wire [3:0] or_2_out;
  wire [15:0] adder_1_out, and_2_out, multiplexer_1_out, not_1_out, or_1_out;

  Multiplexer #(.width(16), .enable("false")) multiplexer_1 (
    .in0(B), .in1(not_1_out), .out(multiplexer_1_out), .sel(and_1_out));
  assign not_1_out = ~B;  // NOT_Gate not_1, 16 bits wide
  and and_1 (and_1_out, ALU_Op[0], ALU_Op[1]);
  Adder #(.width(16)) adder_1 (.a(A), .b(multiplexer_1_out), .out(adder_1_out), .cin(and_1_out));  // open: cout
  assign and_2_out = multiplexer_1_out & A;  // AND_Gate and_2, 16 bits wide
  assign or_1_out = multiplexer_1_out | A;  // OR_Gate or_1, 16 bits wide
  Multiplexer #(.select(2), .width(16), .enable("false")) multiplexer_2 (
    .in0(adder_1_out), .in1(and_2_out), .in2(or_1_out), .in3(adder_1_out), .out(ALU_Out), .sel(ALU_Op));
  assign or_2_out = ALU_Out[3:0] | ALU_Out[7:4] | ALU_Out[11:8] | ALU_Out[15:12];  // OR_Gate or_2, 4 bits wide
  not not_2 (Zero, or_3_out);
  or or_3 (or_3_out, or_2_out[0], or_2_out[1], or_2_out[2], or_2_out[3]);

  assign Negative = ALU_Out[15];

  // Notes on the sheet:
  //   16 Bit ALU
  //   00 = ADD
  //   01 = AND
  //   10 = OR
  //   11 = SUB
  //   sub not B
  //   sub cin
  //   sub
endmodule

module _16x16_bit_Register_File (
  input  [15:0] Data_In,
  input  [3:0] Read_Addr_1,
  input  Write_Enable,
  input  [3:0] Write_Addr,
  input  [3:0] Read_Addr_2,
  input  Clock,
  output [15:0] Read_1_Data,
  output [15:0] Read_2_Data
);

  wire demultiplexer_1_out0, demultiplexer_1_out1, demultiplexer_1_out2, demultiplexer_1_out3,
       demultiplexer_1_out4, demultiplexer_1_out5, demultiplexer_1_out6, demultiplexer_1_out7,
       demultiplexer_1_out8, demultiplexer_1_out9, demultiplexer_1_out10, demultiplexer_1_out11,
       demultiplexer_1_out12, demultiplexer_1_out13, demultiplexer_1_out14, demultiplexer_1_out15;
  wire [15:0] register_1_q, register_2_q, register_3_q, register_4_q, register_5_q, register_6_q,
       register_7_q, register_8_q, register_9_q, register_10_q, register_11_q, register_12_q, register_13_q,
       register_14_q, register_15_q, register_16_q;

  Demultiplexer #(.select(4), .enable("false")) demultiplexer_1 (
    .out0(demultiplexer_1_out0), .out1(demultiplexer_1_out1), .out2(demultiplexer_1_out2),
    .out3(demultiplexer_1_out3), .out4(demultiplexer_1_out4), .out5(demultiplexer_1_out5),
    .out6(demultiplexer_1_out6), .out7(demultiplexer_1_out7), .out8(demultiplexer_1_out8),
    .out9(demultiplexer_1_out9), .out10(demultiplexer_1_out10), .out11(demultiplexer_1_out11),
    .out12(demultiplexer_1_out12), .out13(demultiplexer_1_out13), .out14(demultiplexer_1_out14),
    .out15(demultiplexer_1_out15), .in(Write_Enable), .sel(Write_Addr));
  Register #(.width(16)) register_1 (
    .D(Data_In), .en(demultiplexer_1_out0), .Q(register_1_q), .clk(Clock));  // open: clr
  Register #(.width(16)) register_2 (
    .D(Data_In), .en(demultiplexer_1_out1), .Q(register_2_q), .clk(Clock));  // open: clr
  Register #(.width(16)) register_3 (
    .D(Data_In), .en(demultiplexer_1_out2), .Q(register_3_q), .clk(Clock));  // open: clr
  Register #(.width(16)) register_4 (
    .D(Data_In), .en(demultiplexer_1_out3), .Q(register_4_q), .clk(Clock));  // open: clr
  Register #(.width(16)) register_5 (
    .D(Data_In), .en(demultiplexer_1_out4), .Q(register_5_q), .clk(Clock));  // open: clr
  Register #(.width(16)) register_6 (
    .D(Data_In), .en(demultiplexer_1_out5), .Q(register_6_q), .clk(Clock));  // open: clr
  Register #(.width(16)) register_7 (
    .D(Data_In), .en(demultiplexer_1_out6), .Q(register_7_q), .clk(Clock));  // open: clr
  Register #(.width(16)) register_8 (
    .D(Data_In), .en(demultiplexer_1_out7), .Q(register_8_q), .clk(Clock));  // open: clr
  Register #(.width(16)) register_9 (
    .D(Data_In), .en(demultiplexer_1_out8), .Q(register_9_q), .clk(Clock));  // open: clr
  Register #(.width(16)) register_10 (
    .D(Data_In), .en(demultiplexer_1_out9), .Q(register_10_q), .clk(Clock));  // open: clr
  Register #(.width(16)) register_11 (
    .D(Data_In), .en(demultiplexer_1_out10), .Q(register_11_q), .clk(Clock));  // open: clr
  Register #(.width(16)) register_12 (
    .D(Data_In), .en(demultiplexer_1_out11), .Q(register_12_q), .clk(Clock));  // open: clr
  Register #(.width(16)) register_13 (
    .D(Data_In), .en(demultiplexer_1_out12), .Q(register_13_q), .clk(Clock));  // open: clr
  Register #(.width(16)) register_14 (
    .D(Data_In), .en(demultiplexer_1_out13), .Q(register_14_q), .clk(Clock));  // open: clr
  Register #(.width(16)) register_15 (
    .D(Data_In), .en(demultiplexer_1_out14), .Q(register_15_q), .clk(Clock));  // open: clr
  Register #(.width(16)) register_16 (
    .D(Data_In), .en(demultiplexer_1_out15), .Q(register_16_q), .clk(Clock));  // open: clr
  Multiplexer #(.select(4), .width(16), .enable("false")) multiplexer_1 (
    .in0(register_1_q), .in1(register_2_q), .in2(register_3_q), .in3(register_4_q), .in4(register_5_q),
    .in5(register_6_q), .in6(register_7_q), .in7(register_8_q), .in8(register_9_q), .in9(register_10_q),
    .in10(register_11_q), .in11(register_12_q), .in12(register_13_q), .in13(register_14_q),
    .in14(register_15_q), .in15(register_16_q), .out(Read_1_Data), .sel(Read_Addr_1));
  Multiplexer #(.select(4), .width(16), .enable("false")) multiplexer_2 (
    .in0(register_1_q), .in1(register_2_q), .in2(register_3_q), .in3(register_4_q), .in4(register_5_q),
    .in5(register_6_q), .in6(register_7_q), .in7(register_8_q), .in8(register_9_q), .in9(register_10_q),
    .in10(register_11_q), .in11(register_12_q), .in12(register_13_q), .in13(register_14_q),
    .in14(register_15_q), .in15(register_16_q), .out(Read_2_Data), .sel(Read_Addr_2));

  // Notes on the sheet:
  //   16x16-bit Register File
endmodule

module CLU (
  input  [4:0] opcode,
  input  [3:0] funct,
  output JAL,
  output BNE,
  output BEQ,
  output J,
  output R_I,
  output LW,
  output SW,
  output SLT,
  output [1:0] ALU_op,
  output JR
);

  wire and_2_out, and_3_out, not_1_out, not_2_out, not_4_out, not_5_out, xor_1_out;
  wire [0:0] not_3_out;
  wire [1:0] demultiplexer_1_out0, demultiplexer_1_out1, demultiplexer_2_out0, multiplexer_1_out;

  and and_1 (JAL, opcode[4], opcode[2]);
  Demultiplexer #(.width(2)) demultiplexer_1 (
    .out0(demultiplexer_1_out0), .out1(demultiplexer_1_out1), .in(opcode[1:0]), .sel(opcode[2]));  // open: en
  not not_1 (not_1_out, opcode[4]);
  Multiplexer #(.width(2)) multiplexer_1 (
    .in0(funct[1:0]), .in1(demultiplexer_1_out0), .out(multiplexer_1_out), .sel(opcode[3]));  // open: en
  and and_2 (and_2_out, opcode[2], not_1_out);
  Demultiplexer #(.width(2)) demultiplexer_2 (
    .out0(demultiplexer_2_out0), .out1({SW, LW}), .in(demultiplexer_1_out1), .sel(xor_1_out));  // open: en
  xor xor_1 (xor_1_out, demultiplexer_1_out1[0], demultiplexer_1_out1[1]);
  not not_2 (not_2_out, xor_1_out);
  and and_3 (and_3_out, and_2_out, not_2_out);
  not not_3 (not_3_out[0], demultiplexer_2_out0[0]);
  not not_4 (not_4_out, opcode[3]);
  and and_4 (SLT, not_4_out, funct[2]);
  Multiplexer #(.width(2)) multiplexer_2 (
    .in0(multiplexer_1_out), .in1(2'b11), .out(ALU_op), .sel(and_3_out));  // open: en
  not not_5 (not_5_out, opcode[3]);
  Multiplexer #(.width(2)) multiplexer_3 (
    .in0(2'b00), .in1({demultiplexer_2_out0[1], not_3_out[0]}), .out({BEQ, BNE}), .sel(and_3_out));  // open: en
  and and_5 (JR, not_5_out, funct[3]);

  assign J = opcode[4];
  assign R_I = opcode[3];
endmodule

module Program_Counter (
  input  [15:0] in_1,
  input  CLK,
  input  Reset,
  output [15:0] PC
);

  Register #(.width(16)) register_1 (.D(in_1), .en(1'b1), .Q(PC), .clk(CLK), .clr(Reset));
endmodule

module My_CPU (
  input  CLK,
  input  Reset,
  output [15:0] CPU_Op_Out
);

  wire and_1_out, and_2_out, and_3_out, and_4_out, clu_1_beq, clu_1_bne, clu_1_j, clu_1_jal, clu_1_jr,
       clu_1_lw, clu_1_r_i, clu_1_slt, clu_1_sw, multiplexer_4_out, n16_bit_alu_1_negative,
       n16_bit_alu_1_zero, not_1_out, not_2_out, not_3_out, or_1_out, or_2_out, or_3_out, or_4_out;
  wire [1:0] clu_1_alu_op;
  wire [3:0] multiplexer_5_out, multiplexer_6_out, multiplexer_7_out;
  wire [7:0] ram_1_data;
  wire [15:0] adder_1_out, adder_2_out, bit_extender_1_out, bit_extender_2_out, multiplexer_1_out,
       multiplexer_2_out, multiplexer_3_out, multiplexer_8_out, multiplexer_9_out, multiplexer_10_out,
       multiplexer_12_out, n16_bit_alu_1_alu_out, n16x16_bit_register_file_1_read_1_data,
       n16x16_bit_register_file_1_read_2_data, program_counter_1_pc, ram_2_data;
  wire [15:8] ram_1_data_2;
  wire [20:16] ram_1_data_3;

  Multiplexer #(.width(16)) multiplexer_1 (
    .in0(adder_1_out), .in1(adder_2_out), .out(multiplexer_1_out), .sel(or_4_out));  // open: en
  or or_1 (or_1_out, clu_1_j, clu_1_jr);
  Multiplexer #(.width(16)) multiplexer_2 (
    .in0(multiplexer_1_out), .in1(multiplexer_3_out), .out(multiplexer_2_out), .sel(or_1_out));  // open: en
  // Probe on program_counter_1_pc
  Program_Counter program_counter_1 (.CLK(CLK), .Reset(Reset), .PC(program_counter_1_pc), .in_1(multiplexer_2_out));
  Adder #(.width(16)) adder_1 (.a(program_counter_1_pc), .b(16'h1), .out(adder_1_out));  // open: cin, cout
  Multiplexer #(.width(16)) multiplexer_3 (
    .in0({ram_1_data_2, ram_1_data}), .in1(n16x16_bit_register_file_1_read_1_data), .out(multiplexer_3_out),
    .sel(clu_1_jr));  // open: en
  // Probe on {ram_1_data_2, ram_1_data}
  // Probe on {ram_1_data_3, ram_1_data_2, ram_1_data}
  RAM #(.addrWidth(16), .dataWidth(21)) ram_1 (
    .addr(program_counter_1_pc), .data({ram_1_data_3, ram_1_data_2, ram_1_data}));  // open: sel, clk, ld, clr
  CLU clu_1 (
    .opcode(ram_1_data_3), .funct(ram_1_data[3:0]), .J(clu_1_j), .R_I(clu_1_r_i), .LW(clu_1_lw),
    .SW(clu_1_sw), .SLT(clu_1_slt), .ALU_op(clu_1_alu_op), .BNE(clu_1_bne), .BEQ(clu_1_beq), .JAL(clu_1_jal),
    .JR(clu_1_jr));
  Multiplexer multiplexer_4 (.in0(1'b1), .in1(1'b0), .out(multiplexer_4_out), .sel(clu_1_sw));  // open: en
  Multiplexer #(.width(4)) multiplexer_5 (
    .in0(ram_1_data[7:4]), .in1(ram_1_data_2[15:12]), .out(multiplexer_5_out), .sel(or_2_out));  // open: en
  or or_2 (or_2_out, clu_1_sw, or_3_out);
  Multiplexer #(.width(4)) multiplexer_6 (
    .in0(ram_1_data_2[11:8]), .in1(4'b0000), .out(multiplexer_6_out), .sel(clu_1_jal));  // open: en
  // Probe on nothing
  Multiplexer #(.width(4)) multiplexer_7 (
    .in0(ram_1_data_2[15:12]), .in1(4'b1110), .out(multiplexer_7_out), .sel(clu_1_jal));  // open: en
  // Probe on nothing
  _16x16_bit_Register_File u_16x16_bit_register_file_1 (
    .Data_In(multiplexer_9_out), .Write_Enable(multiplexer_4_out), .Clock(CLK),
    .Read_1_Data(n16x16_bit_register_file_1_read_1_data),
    .Read_2_Data(n16x16_bit_register_file_1_read_2_data), .Write_Addr(multiplexer_7_out),
    .Read_Addr_1(multiplexer_6_out), .Read_Addr_2(multiplexer_5_out));
  assign bit_extender_1_out = {{8{ram_1_data[7]}}, ram_1_data};  // Bit_Extender bit_extender_1
  or or_3 (or_3_out, clu_1_jr, clu_1_bne, clu_1_beq, and_1_out);
  and and_1 (and_1_out, clu_1_j, not_1_out);
  not not_1 (not_1_out, clu_1_jal);
  // Probe on multiplexer_9_out
  Multiplexer #(.width(16)) multiplexer_8 (
    .in0(n16x16_bit_register_file_1_read_2_data), .in1(bit_extender_1_out), .out(multiplexer_8_out),
    .sel(and_2_out));  // open: en
  and and_2 (and_2_out, clu_1_r_i, not_2_out);
  not not_2 (not_2_out, or_3_out);
  // Probe on nothing
  Multiplexer #(.width(16)) multiplexer_9 (
    .in0(multiplexer_12_out), .in1(ram_2_data), .out(multiplexer_9_out), .sel(clu_1_lw));  // open: en
  Multiplexer #(.width(16)) multiplexer_10 (
    .in0(multiplexer_8_out), .in1(adder_1_out), .out(multiplexer_10_out), .sel(clu_1_jal));  // open: en
  Adder #(.width(16)) adder_2 (.a(bit_extender_1_out), .b(adder_1_out), .out(adder_2_out));  // open: cin, cout
  _16_bit_ALU u_16_bit_alu_1 (
    .A(n16x16_bit_register_file_1_read_1_data), .B(multiplexer_10_out), .ALU_Out(n16_bit_alu_1_alu_out),
    .ALU_Op(clu_1_alu_op), .Zero(n16_bit_alu_1_zero), .Negative(n16_bit_alu_1_negative));
  assign bit_extender_2_out = {{15{1'b0}}, n16_bit_alu_1_negative};  // Bit_Extender bit_extender_2
  and and_3 (and_3_out, n16_bit_alu_1_zero, clu_1_beq);
  not not_3 (not_3_out, n16_bit_alu_1_zero);
  and and_4 (and_4_out, not_3_out, clu_1_bne);
  or or_4 (or_4_out, and_3_out, and_4_out);
  Multiplexer #(.width(16)) multiplexer_11 (
    .in0(n16_bit_alu_1_alu_out), .in1(bit_extender_2_out), .out(CPU_Op_Out), .sel(clu_1_slt));  // open: en
  // Probe on nothing
  Multiplexer #(.width(16)) multiplexer_12 (
    .in0(CPU_Op_Out), .in1(n16x16_bit_register_file_1_read_2_data), .out(multiplexer_12_out), .sel(or_3_out));  // open: en
  RAM #(.addrWidth(16), .dataWidth(16), .bus("separate")) ram_2 (
    .addr(multiplexer_12_out), .din(n16x16_bit_register_file_1_read_2_data), .data(ram_2_data),
    .str(clu_1_sw), .sel(1'b1), .clk(CLK), .ld(clu_1_lw), .clr(1'b0));

  // Notes on the sheet:
  //   Branch
  //   Jump
  //   PC+1
  //   PCJump
  //   dest
  //   src1
  //   src2
  //   imm I-type
  //   PCBranch
  //   PCSrc
endmodule
