// Logisim project Lab 2.circ as structural Verilog
module XOR_gate (
  input  X,
  input  Y,
  output out_3
);

  wire and_1_out, and_2_out, not_1_out, not_2_out;

  not not_1 (not_1_out, X);
  and and_1 (and_1_out, not_1_out, Y);
  and and_2 (and_2_out, X, not_2_out);
  not not_2 (not_2_out, Y);
  or or_1 (out_3, and_1_out, and_2_out);
endmodule

module Half_Adder (
  input  A,
  input  B,
  output S,
  output C_out
);

  XOR_gate xor_gate_1 (.Y(A), .out_3(S), .X(B));
  and and_1 (C_out, A, B);
endmodule

module Full_Adder (
  input  A,
  input  B,
  input  C_in,
  output S,
  output C_out
);

  wire half_adder_1_c_out, half_adder_1_s, half_adder_2_c_out;

  Half_Adder half_adder_1 (.A(A), .B(B), .S(half_adder_1_s), .C_out(half_adder_1_c_out));
  Half_Adder half_adder_2 (.A(half_adder_1_s), .B(C_in), .S(S), .C_out(half_adder_2_c_out));
  or or_1 (C_out, half_adder_2_c_out, half_adder_1_c_out);
endmodule

module _2_MUX (
  input  A,
  input  B,
  input  S,
  output Output
);

  wire and_1_out, and_2_out, not_1_out;

  and and_1 (and_1_out, A, not_1_out);
  not not_1 (not_1_out, S);
  and and_2 (and_2_out, B, S);
  or or_1 (Output, and_1_out, and_2_out);
endmodule

module _4_MUX (
  input  A,
  input  B,
  input  C,
  input  D,
  input  S_1,
  input  S_0,
  output Output
);

  wire n2_mux_1_output, n2_mux_2_output;

  _2_MUX u_2_mux_1 (.A(A), .B(B), .S(S_0), .Output(n2_mux_1_output));
  _2_MUX u_2_mux_2 (.A(C), .B(D), .S(S_0), .Output(n2_mux_2_output));
  _2_MUX u_2_mux_3 (.A(n2_mux_1_output), .B(n2_mux_2_output), .S(S_1), .Output(Output));
endmodule

module _1_Bit_ALU (
  input  A,
  input  B,
  input  C_in,
  input  S_1,
  input  S_0,
  output C_out,
  output out_7
);

  wire and_1_out, full_adder_1_s, or_1_out;

  Full_Adder full_adder_1 (.A(A), .B(B), .C_in(C_in), .S(full_adder_1_s), .C_out(C_out));
  and and_1 (and_1_out, A, B);
  _4_MUX u_4_mux_1 (.A(full_adder_1_s), .B(and_1_out), .C(or_1_out), .S_1(S_1), .S_0(S_0), .Output(out_7));  // open: D
  or or_1 (or_1_out, A, B);
endmodule

module _4_Bit_Ripple (
  input  A_3,
  input  B_3,
  input  A_2,
  input  B_2,
  input  A_1,
  input  B_1,
  input  A_0,
  input  B_0,
  input  S_1,
  input  S_0,
  output C_out,
  output out_12,
  output out_13,
  output out_14,
  output out_15
);

  wire and_1_out, n1_bit_alu_2_c_out, n1_bit_alu_3_c_out, n1_bit_alu_4_c_out;

  _1_Bit_ALU u_1_bit_alu_1 (
    .S_1(S_1), .S_0(S_0), .A(A_3), .B(B_3), .out_7(out_12), .C_in(n1_bit_alu_2_c_out), .C_out(C_out));
  _1_Bit_ALU u_1_bit_alu_2 (
    .S_1(S_1), .S_0(S_0), .A(A_2), .B(B_2), .out_7(out_13), .C_in(n1_bit_alu_3_c_out),
    .C_out(n1_bit_alu_2_c_out));
  _1_Bit_ALU u_1_bit_alu_3 (
    .S_1(S_1), .S_0(S_0), .A(A_1), .B(B_1), .out_7(out_14), .C_in(n1_bit_alu_4_c_out),
    .C_out(n1_bit_alu_3_c_out));
  _1_Bit_ALU u_1_bit_alu_4 (
    .S_1(S_1), .S_0(S_0), .A(A_0), .B(B_0), .out_7(out_15), .C_in(and_1_out), .C_out(n1_bit_alu_4_c_out));
  and and_1 (and_1_out, S_1, S_0);
endmodule

module Full_1_Bit_ALU (
  input  A,
  input  B,
  input  C_in,
  input  S_1,
  input  S_0,
  output C_out,
  output out_7
);

  wire and_1_out, and_2_out, full_adder_1_s, n2_mux_1_output, not_1_out, or_1_out;

  and and_1 (and_1_out, S_1, S_0);
  _2_MUX u_2_mux_1 (.A(B), .B(not_1_out), .S(and_1_out), .Output(n2_mux_1_output));
  Full_Adder full_adder_1 (.A(A), .B(n2_mux_1_output), .C_in(C_in), .S(full_adder_1_s), .C_out(C_out));
  not not_1 (not_1_out, B);
  and and_2 (and_2_out, A, B);
  _4_MUX u_4_mux_1 (
    .A(full_adder_1_s), .B(and_2_out), .C(or_1_out), .D(full_adder_1_s), .S_1(S_1), .S_0(S_0), .Output(out_7));
  or or_1 (or_1_out, A, B);
endmodule

module Full_4_Bit_ALU (
  input  A_3,
  input  B_3,
  input  A_2,
  input  B_2,
  input  A_1,
  input  B_1,
  input  A_0,
  input  B_0,
  input  S_1,
  input  S_0,
  output C_out,
  output out_12,
  output out_13,
  output out_14,
  output out_15
);

  wire and_1_out, full_1_bit_alu_2_c_out, full_1_bit_alu_3_c_out, full_1_bit_alu_4_c_out;

  Full_1_Bit_ALU full_1_bit_alu_1 (
    .A(A_3), .B(B_3), .C_out(C_out), .C_in(full_1_bit_alu_2_c_out), .S_1(S_1), .S_0(S_0), .out_7(out_12));
  Full_1_Bit_ALU full_1_bit_alu_2 (
    .A(A_2), .B(B_2), .C_out(full_1_bit_alu_2_c_out), .C_in(full_1_bit_alu_3_c_out), .S_1(S_1), .S_0(S_0),
    .out_7(out_13));
  Full_1_Bit_ALU full_1_bit_alu_3 (
    .A(A_1), .B(B_1), .C_out(full_1_bit_alu_3_c_out), .C_in(full_1_bit_alu_4_c_out), .S_1(S_1), .S_0(S_0),
    .out_7(out_14));
  Full_1_Bit_ALU full_1_bit_alu_4 (
    .A(A_0), .B(B_0), .C_out(full_1_bit_alu_4_c_out), .C_in(and_1_out), .S_1(S_1), .S_0(S_0), .out_7(out_15));
  and and_1 (and_1_out, S_1, S_0);
endmodule
