// Logisim project Lab 3.circ as structural Verilog
module SR_Latch (
  input  R,
  input  S,
  output Q,
  output Q_bar
);

  nor nor_1 (Q, R, Q_bar);
  nor nor_2 (Q_bar, Q, S);
endmodule

module D_Latch (
  input  D,
  input  E,
  output Q
);

  wire and_1_out, and_2_out, not_1_out;

  not not_1 (not_1_out, D);
  and and_1 (and_1_out, not_1_out, E);
  and and_2 (and_2_out, D, E);
  SR_Latch sr_latch_1 (.R(and_1_out), .S(and_2_out), .Q(Q));  // open: Q_bar
endmodule

module D_Flip_flop (
  input  D,
  input  CLK,
  output Output
);

  wire d_latch_1_q, not_1_out;

  not not_1 (not_1_out, CLK);
  D_Latch d_latch_1 (.D(D), .E(not_1_out), .Q(d_latch_1_q));
  D_Latch d_latch_2 (.D(d_latch_1_q), .E(CLK), .Q(Output));

  // Notes on the sheet:
  //   Master
  //   Slave
endmodule

module Enabled_Flip_flop (
  input  D,
  input  E,
  input  CLK,
  output Q
);

  wire n2_mux_1_p4;

  // _2_MUX 2_mux_1: pin names not known; wires that end beside it: Q, D, E, n2_mux_1_p4
  D_Flip_flop d_flip_flop_1 (.D(n2_mux_1_p4), .CLK(CLK), .Output(Q));
endmodule

module _4_Bit_Register (
  input  [3:0] D,
  input  CLK,
  input  E,
  output [3:0] Q
);

  Enabled_Flip_flop enabled_flip_flop_1 (.D(D[0]), .E(E), .Q(Q[0]), .CLK(CLK));
  Enabled_Flip_flop enabled_flip_flop_2 (.D(D[1]), .E(E), .Q(Q[1]), .CLK(CLK));
  Enabled_Flip_flop enabled_flip_flop_3 (.D(D[2]), .E(E), .Q(Q[2]), .CLK(CLK));
  Enabled_Flip_flop enabled_flip_flop_4 (.D(D[3]), .E(E), .Q(Q[3]), .CLK(CLK));
endmodule

module _2_DEMUX (
  input  Input,
  input  S,
  output _0,
  output _1
);

  wire not_1_out;

  and and_1 (_0, Input, not_1_out);
  not not_1 (not_1_out, S);
  and and_2 (_1, Input, S);
endmodule

module _4_DEMUX (
  input  in_1,
  input  [1:0] S,
  output _0,
  output _1,
  output _2,
  output _3
);

  wire n2_demux_1__0, n2_demux_1__1;

  _2_DEMUX u_2_demux_1 (.Input(in_1), ._0(n2_demux_1__0), ._1(n2_demux_1__1), .S(S[1]));
  _2_DEMUX u_2_demux_2 (.Input(n2_demux_1__0), ._0(_0), ._1(_1), .S(S[0]));
  _2_DEMUX u_2_demux_3 (.Input(n2_demux_1__1), ._0(_2), ._1(_3), .S(S[0]));
endmodule

module _8_DEMUX (
  input  in_1,
  input  [2:0] S,
  output _0,
  output _1,
  output _2,
  output _3,
  output _4,
  output _5,
  output _6,
  output _7
);

  wire n2_demux_1__0, n2_demux_1__1;

  _2_DEMUX u_2_demux_1 (.Input(in_1), ._0(n2_demux_1__0), ._1(n2_demux_1__1), .S(S[2]));
  _4_DEMUX u_4_demux_1 (.in_1(n2_demux_1__0), .S(S[1:0]), ._0(_0), ._1(_1), ._2(_2), ._3(_3));
  _4_DEMUX u_4_demux_2 (.in_1(n2_demux_1__1), .S(S[1:0]), ._0(_4), ._1(_5), ._2(_6), ._3(_7));
endmodule

module _4_Bit_2_MUX (
  input  in_1,
  input  in_2,
  input  in_3,
  input  in_4,
  input  in_5,
  input  in_6,
  input  in_7,
  input  in_8,
  input  in_9,
  output [3:0] out_10
);

  // _2_MUX 2_mux_1: pin names not known; wires that end beside it: in_1, in_2, in_9, out_10[0]
  // _2_MUX 2_mux_2: pin names not known; wires that end beside it: in_3, in_4, in_9, out_10[1]
  // _2_MUX 2_mux_3: pin names not known; wires that end beside it: in_5, in_6, in_9, out_10[2]
  // _2_MUX 2_mux_4: pin names not known; wires that end beside it: in_7, in_8, in_9, out_10[3]
endmodule

module _4_Bit_4_MUX (
  input  [3:0] A,
  input  [3:0] B,
  input  [3:0] C,
  input  [3:0] D,
  input  [1:0] S,
  output [3:0] out_6
);

  wire [3:0] n4_bit_2_mux_1_out_10, n4_bit_2_mux_2_out_10;

  _4_Bit_2_MUX u_4_bit_2_mux_1 (
    .in_1(A[0]), .in_2(B[0]), .in_3(A[1]), .in_4(B[1]), .in_5(A[2]), .in_6(B[2]), .in_7(A[3]), .in_8(B[3]),
    .in_9(S[0]), .out_10(n4_bit_2_mux_1_out_10));
  _4_Bit_2_MUX u_4_bit_2_mux_2 (
    .in_1(C[0]), .in_2(D[0]), .in_3(C[1]), .in_4(D[1]), .in_5(C[2]), .in_6(D[2]), .in_7(C[3]), .in_8(D[3]),
    .in_9(S[0]), .out_10(n4_bit_2_mux_2_out_10));
  _4_Bit_2_MUX u_4_bit_2_mux_3 (
    .in_1(n4_bit_2_mux_1_out_10[0]), .in_2(n4_bit_2_mux_2_out_10[0]), .in_3(n4_bit_2_mux_1_out_10[1]),
    .in_4(n4_bit_2_mux_2_out_10[1]), .in_5(n4_bit_2_mux_1_out_10[2]), .in_6(n4_bit_2_mux_2_out_10[2]),
    .in_7(n4_bit_2_mux_1_out_10[3]), .in_8(n4_bit_2_mux_2_out_10[3]), .in_9(S[1]), .out_10(out_6));
endmodule

module _4_Bit_8_MUX (
  input  [3:0] _7,
  input  [3:0] _6,
  input  [3:0] _5,
  input  [3:0] _4,
  input  [3:0] _3,
  input  [3:0] _2,
  input  [3:0] _1,
  input  [3:0] _0,
  input  [2:0] S,
  output [3:0] out_10
);

  wire [3:0] n4_bit_4_mux_1_out_6, n4_bit_4_mux_2_out_6;

  _4_Bit_4_MUX u_4_bit_4_mux_1 (.A(_4), .B(_5), .C(_6), .D(_7), .S(S[1:0]), .out_6(n4_bit_4_mux_1_out_6));
  _4_Bit_4_MUX u_4_bit_4_mux_2 (.A(_0), .B(_1), .C(_2), .D(_3), .S(S[1:0]), .out_6(n4_bit_4_mux_2_out_6));
  _4_Bit_2_MUX u_4_bit_2_mux_1 (
    .in_1(n4_bit_4_mux_2_out_6[0]), .in_2(n4_bit_4_mux_1_out_6[0]), .in_3(n4_bit_4_mux_2_out_6[1]),
    .in_4(n4_bit_4_mux_1_out_6[1]), .in_5(n4_bit_4_mux_2_out_6[2]), .in_6(n4_bit_4_mux_1_out_6[2]),
    .in_7(n4_bit_4_mux_2_out_6[3]), .in_8(n4_bit_4_mux_1_out_6[3]), .in_9(S[2]), .out_10(out_10));
endmodule

module Register_File (
  input  [3:0] D,
  input  WE,
  input  [2:0] WA,
  input  CLK,
  input  [2:0] RA_1,
  input  [2:0] RA_2,
  output [3:0] out_7,
  output [3:0] out_8
);

  wire n8_demux_1__0, n8_demux_1__1, n8_demux_1__2, n8_demux_1__3, n8_demux_1__4, n8_demux_1__5,
       n8_demux_1__6, n8_demux_1__7;
  wire [3:0] n4_bit_register_1_q, n4_bit_register_2_q, n4_bit_register_3_q, n4_bit_register_4_q,
       n4_bit_register_5_q, n4_bit_register_6_q, n4_bit_register_7_q, n4_bit_register_8_q;

  _8_DEMUX u_8_demux_1 (
    .in_1(WE), .S(WA), ._0(n8_demux_1__0), ._1(n8_demux_1__1), ._2(n8_demux_1__2), ._3(n8_demux_1__3),
    ._4(n8_demux_1__4), ._5(n8_demux_1__5), ._6(n8_demux_1__6), ._7(n8_demux_1__7));
  _4_Bit_Register u_4_bit_register_1 (.D(D), .CLK(CLK), .E(n8_demux_1__0), .Q(n4_bit_register_1_q));
  _4_Bit_Register u_4_bit_register_2 (.D(D), .CLK(CLK), .E(n8_demux_1__1), .Q(n4_bit_register_2_q));
  _4_Bit_Register u_4_bit_register_3 (.D(D), .CLK(CLK), .E(n8_demux_1__2), .Q(n4_bit_register_3_q));
  _4_Bit_Register u_4_bit_register_4 (.D(D), .CLK(CLK), .E(n8_demux_1__3), .Q(n4_bit_register_4_q));
  _4_Bit_Register u_4_bit_register_5 (.D(D), .CLK(CLK), .E(n8_demux_1__4), .Q(n4_bit_register_5_q));
  _4_Bit_Register u_4_bit_register_6 (.D(D), .CLK(CLK), .E(n8_demux_1__5), .Q(n4_bit_register_6_q));
  _4_Bit_Register u_4_bit_register_7 (.D(D), .CLK(CLK), .E(n8_demux_1__6), .Q(n4_bit_register_7_q));
  _4_Bit_Register u_4_bit_register_8 (.D(D), .CLK(CLK), .E(n8_demux_1__7), .Q(n4_bit_register_8_q));
  // Probe on n4_bit_register_1_q
  // Probe on n4_bit_register_8_q
  // Probe on n4_bit_register_2_q
  _4_Bit_8_MUX u_4_bit_8_mux_1 (
    ._7(n4_bit_register_8_q), ._6(n4_bit_register_7_q), ._5(n4_bit_register_6_q), ._4(n4_bit_register_5_q),
    ._3(n4_bit_register_4_q), ._2(n4_bit_register_3_q), ._1(n4_bit_register_2_q), ._0(n4_bit_register_1_q),
    .S(RA_1), .out_10(out_7));
  _4_Bit_8_MUX u_4_bit_8_mux_2 (
    ._7(n4_bit_register_8_q), ._6(n4_bit_register_7_q), ._5(n4_bit_register_6_q), ._4(n4_bit_register_5_q),
    ._3(n4_bit_register_4_q), ._2(n4_bit_register_3_q), ._1(n4_bit_register_2_q), ._0(n4_bit_register_1_q),
    .S(RA_2), .out_10(out_8));
endmodule

module Datapath (
  input  [11:0] instruction_word,
  input  CLK,
  input  WE
);

  wire [3:0] bit_extender_1_out, full_4_bit_alu_1_p11, n4_bit_2_mux_1_out_10, register_file_1_out_7,
       register_file_1_out_8;

  Register_File register_file_1 (
    .D(full_4_bit_alu_1_p11), .WE(WE), .RA_1(instruction_word[5:3]), .RA_2(instruction_word[2:0]),
    .out_7(register_file_1_out_7), .out_8(register_file_1_out_8), .WA(instruction_word[8:6]), .CLK(CLK));
  assign bit_extender_1_out = {{1{instruction_word[2]}}, instruction_word[2:0]};  // Bit_Extender bit_extender_1
  _4_Bit_2_MUX u_4_bit_2_mux_1 (
    .in_1(register_file_1_out_8[0]), .in_2(bit_extender_1_out[0]), .in_3(register_file_1_out_8[1]),
    .in_4(bit_extender_1_out[1]), .in_5(register_file_1_out_8[2]), .in_6(bit_extender_1_out[2]),
    .in_7(register_file_1_out_8[3]), .in_8(bit_extender_1_out[3]), .in_9(instruction_word[11]),
    .out_10(n4_bit_2_mux_1_out_10));
  // Full_4_Bit_ALU full_4_bit_alu_1: pin names not known; wires that end beside it: register_file_1_out_7[0], register_file_1_out_7[1], register_file_1_out_7[2], register_file_1_out_7[3], n4_bit_2_mux_1_out_10[0], n4_bit_2_mux_1_out_10[1], n4_bit_2_mux_1_out_10[2], n4_bit_2_mux_1_out_10[3], instruction_word[9], instruction_word[10], full_4_bit_alu_1_p11[0], full_4_bit_alu_1_p11[1], full_4_bit_alu_1_p11[2], full_4_bit_alu_1_p11[3]
endmodule
