// Logisim project Lab 4 - memory.circ as structural Verilog
module _4_bit_ALU (
  input  [3:0] A,
  input  [3:0] B,
  input  [1:0] ALU_Op,
  output [3:0] ALU_Out
);

  wire and_1_out;
  wire [3:0] adder_1_out, and_2_out, multiplexer_1_out, not_1_out, or_1_out;

  Multiplexer #(.width(4), .enable("false")) multiplexer_1 (
    .in0(B), .in1(not_1_out), .out(multiplexer_1_out), .sel(and_1_out));
  assign not_1_out = ~B;  // NOT_Gate not_1, 4 bits wide
  and and_1 (and_1_out, ALU_Op[0], ALU_Op[1]);
  Adder #(.width(4)) adder_1 (.a(A), .b(multiplexer_1_out), .out(adder_1_out), .cin(and_1_out));  // open: cout
  assign and_2_out = multiplexer_1_out & A;  // AND_Gate and_2, 4 bits wide
  assign or_1_out = multiplexer_1_out | A;  // OR_Gate or_1, 4 bits wide
  Multiplexer #(.select(2), .width(4), .enable("false")) multiplexer_2 (
    .in0(adder_1_out), .in1(and_2_out), .in2(or_1_out), .in3(adder_1_out), .out(ALU_Out), .sel(ALU_Op));

  // Notes on the sheet:
  //   4 Bit ALU
  //   00 = ADD
  //   01 = AND
  //   10 = OR
  //   11 = SUB
  //   sub not B
  //   sub cin
  //   sub
endmodule

module _8x4_bit_Register_File (
  input  [3:0] Data_In,
  input  [2:0] Read_Addr_1,
  input  Write_Enable,
  input  [2:0] Write_Addr,
  input  [2:0] Read_Addr_2,
  input  Clock,
  output [3:0] Read_1_Data,
  output [3:0] Read_2_Data
);

  wire demultiplexer_1_out0, demultiplexer_1_out1, demultiplexer_1_out2, demultiplexer_1_out3,
       demultiplexer_1_out4, demultiplexer_1_out5, demultiplexer_1_out6, demultiplexer_1_out7;
  wire [3:0] register_1_q, register_2_q, register_3_q, register_4_q, register_5_q, register_6_q,
       register_7_q, register_8_q;

  Demultiplexer #(.select(3), .enable("false")) demultiplexer_1 (
    .out0(demultiplexer_1_out0), .out1(demultiplexer_1_out1), .out2(demultiplexer_1_out2),
    .out3(demultiplexer_1_out3), .out4(demultiplexer_1_out4), .out5(demultiplexer_1_out5),
    .out6(demultiplexer_1_out6), .out7(demultiplexer_1_out7), .in(Write_Enable), .sel(Write_Addr));
  Register #(.width(4)) register_1 (
    .D(Data_In), .en(demultiplexer_1_out0), .Q(register_1_q), .clk(Clock));  // open: clr
  Register #(.width(4)) register_2 (
    .D(Data_In), .en(demultiplexer_1_out1), .Q(register_2_q), .clk(Clock));  // open: clr
  Register #(.width(4)) register_3 (
    .D(Data_In), .en(demultiplexer_1_out2), .Q(register_3_q), .clk(Clock));  // open: clr
  Register #(.width(4)) register_4 (
    .D(Data_In), .en(demultiplexer_1_out3), .Q(register_4_q), .clk(Clock));  // open: clr
  Register #(.width(4)) register_5 (
    .D(Data_In), .en(demultiplexer_1_out4), .Q(register_5_q), .clk(Clock));  // open: clr
  Register #(.width(4)) register_6 (
    .D(Data_In), .en(demultiplexer_1_out5), .Q(register_6_q), .clk(Clock));  // open: clr
  Register #(.width(4)) register_7 (
    .D(Data_In), .en(demultiplexer_1_out6), .Q(register_7_q), .clk(Clock));  // open: clr
  Register #(.width(4)) register_8 (
    .D(Data_In), .en(demultiplexer_1_out7), .Q(register_8_q), .clk(Clock));  // open: clr
  Multiplexer #(.select(3), .width(4), .enable("false")) multiplexer_1 (
    .in0(register_1_q), .in1(register_2_q), .in2(register_3_q), .in3(register_4_q), .in4(register_5_q),
    .in5(register_6_q), .in6(register_7_q), .in7(register_8_q), .out(Read_1_Data), .sel(Read_Addr_1));
  Multiplexer #(.select(3), .width(4), .enable("false")) multiplexer_2 (
    .in0(register_1_q), .in1(register_2_q), .in2(register_3_q), .in3(register_4_q), .in4(register_5_q),
    .in5(register_6_q), .in6(register_7_q), .in7(register_8_q), .out(Read_2_Data), .sel(Read_Addr_2));

  // Notes on the sheet:
  //   8x4-bit Register File
endmodule

module ALU_REG_Instruction (
  input  [13:0] dest,
  input  CLK,
  output [3:0] CPU_Op_Out
);

  wire [3:0] bit_extender_1_out, multiplexer_1_out, n8x4_bit_register_file_1_read_1_data,
       n8x4_bit_register_file_1_read_2_data;

  _8x4_bit_Register_File u_8x4_bit_register_file_1 (
    .Read_Addr_2(dest[2:0]), .Data_In(CPU_Op_Out), .Read_1_Data(n8x4_bit_register_file_1_read_1_data),
    .Read_Addr_1(dest[5:3]), .Write_Enable(1'b1), .Write_Addr(dest[8:6]),
    .Read_2_Data(n8x4_bit_register_file_1_read_2_data), .Clock(CLK));
  assign bit_extender_1_out = {{1{dest[2]}}, dest[2:0]};  // Bit_Extender bit_extender_1
  _4_bit_ALU u_4_bit_alu_1 (
    .A(n8x4_bit_register_file_1_read_1_data), .ALU_Out(CPU_Op_Out), .B(multiplexer_1_out), .ALU_Op(dest[10:9]));
  Multiplexer #(.width(4), .enable("false")) multiplexer_1 (
    .in0(n8x4_bit_register_file_1_read_2_data), .in1(bit_extender_1_out), .out(multiplexer_1_out),
    .sel(dest[13]));

  // Notes on the sheet:
  //   op
  //   SW
  //   R/I
  //   LW
  //   src1
  //   dest
  //   src2
  //   src2
  //   dest
  //   src1
  //   immed data
  //   immed select
  //   ALU op
endmodule

module ALU_With_Mem (
  input  [13:0] dest,
  input  CLK,
  output [3:0] CPU_Op_Out
);

  wire multiplexer_1_out;
  wire [2:0] multiplexer_2_out;
  wire [3:0] bit_extender_1_out, multiplexer_3_out, multiplexer_4_out, n8x4_bit_register_file_1_read_1_data,
       n8x4_bit_register_file_1_read_2_data, ram_1_data;

  Multiplexer multiplexer_1 (.in0(1'b1), .in1(1'b0), .out(multiplexer_1_out), .sel(dest[12]));  // open: en
  Multiplexer #(.width(3)) multiplexer_2 (
    .in0(dest[2:0]), .in1(dest[8:6]), .out(multiplexer_2_out), .sel(dest[12]));  // open: en
  _8x4_bit_Register_File u_8x4_bit_register_file_1 (
    .Read_Addr_2(multiplexer_2_out), .Data_In(multiplexer_3_out),
    .Read_1_Data(n8x4_bit_register_file_1_read_1_data), .Read_Addr_1(dest[5:3]),
    .Write_Enable(multiplexer_1_out), .Write_Addr(dest[8:6]),
    .Read_2_Data(n8x4_bit_register_file_1_read_2_data), .Clock(CLK));
  // Probe on multiplexer_4_out
  assign bit_extender_1_out = {{1{dest[2]}}, dest[2:0]};  // Bit_Extender bit_extender_1
  Multiplexer #(.width(4)) multiplexer_3 (
    .in0(CPU_Op_Out), .in1(ram_1_data), .out(multiplexer_3_out), .sel(dest[11]));  // open: en
  Multiplexer #(.width(4), .enable("false")) multiplexer_4 (
    .in0(n8x4_bit_register_file_1_read_2_data), .in1(bit_extender_1_out), .out(multiplexer_4_out),
    .sel(dest[13]));
  _4_bit_ALU u_4_bit_alu_1 (
    .A(n8x4_bit_register_file_1_read_1_data), .ALU_Out(CPU_Op_Out), .B(multiplexer_4_out), .ALU_Op(dest[10:9]));
  RAM #(.addrWidth(4), .dataWidth(4), .bus("separate")) ram_1 (
    .addr(CPU_Op_Out), .din(n8x4_bit_register_file_1_read_2_data), .data(ram_1_data), .str(dest[12]),
    .sel(1'b1), .clk(CLK), .ld(dest[11]), .clr(1'b0));

  // Notes on the sheet:
  //   op
  //   SW
  //   R/I
  //   LW
  //   dest
  //   src1
  //   src2
  //   src2
  //   dest
  //   src1
  //   immed data
  //   immed select
  //   ALU op
endmodule

module CLU (
  input  [4:0] Opcode,
  output [1:0] ALU_op,
  output LW,
  output SW,
  output R_I
);


  assign ALU_op = Opcode[1:0];
  assign LW = Opcode[2];
  assign R_I = Opcode[4];
  assign SW = Opcode[3];
endmodule

module ALU_with_Mem_and_Control (
  input  [13:0] dest,
  input  CLK,
  output [3:0] CPU_Op_Out
);

  wire clu_1_lw, clu_1_r_i, clu_1_sw, multiplexer_1_out;
  wire [1:0] clu_1_alu_op;
  wire [2:0] multiplexer_2_out;
  wire [3:0] bit_extender_1_out, multiplexer_3_out, multiplexer_4_out, n8x4_bit_register_file_1_read_1_data,
       n8x4_bit_register_file_1_read_2_data, ram_1_data;

  CLU clu_1 (.Opcode(dest[13:9]), .ALU_op(clu_1_alu_op), .LW(clu_1_lw), .SW(clu_1_sw), .R_I(clu_1_r_i));
  Multiplexer multiplexer_1 (.in0(1'b1), .in1(1'b0), .out(multiplexer_1_out), .sel(clu_1_sw));  // open: en
  Multiplexer #(.width(3)) multiplexer_2 (
    .in0(dest[2:0]), .in1(dest[8:6]), .out(multiplexer_2_out), .sel(clu_1_sw));  // open: en
  _8x4_bit_Register_File u_8x4_bit_register_file_1 (
    .Read_Addr_2(multiplexer_2_out), .Data_In(multiplexer_3_out),
    .Read_1_Data(n8x4_bit_register_file_1_read_1_data), .Read_Addr_1(dest[5:3]),
    .Write_Enable(multiplexer_1_out), .Write_Addr(dest[8:6]),
    .Read_2_Data(n8x4_bit_register_file_1_read_2_data), .Clock(CLK));
  assign bit_extender_1_out = {{1{dest[2]}}, dest[2:0]};  // Bit_Extender bit_extender_1
  Multiplexer #(.width(4)) multiplexer_3 (
    .in0(CPU_Op_Out), .in1(ram_1_data), .out(multiplexer_3_out), .sel(clu_1_lw));  // open: en
  Multiplexer #(.width(4), .enable("false")) multiplexer_4 (
    .in0(n8x4_bit_register_file_1_read_2_data), .in1(bit_extender_1_out), .out(multiplexer_4_out),
    .sel(clu_1_r_i));
  _4_bit_ALU u_4_bit_alu_1 (
    .A(n8x4_bit_register_file_1_read_1_data), .ALU_Out(CPU_Op_Out), .B(multiplexer_4_out),
    .ALU_Op(clu_1_alu_op));
  RAM #(.addrWidth(4), .dataWidth(4), .bus("separate")) ram_1 (
    .addr(CPU_Op_Out), .din(n8x4_bit_register_file_1_read_2_data), .data(ram_1_data), .str(clu_1_sw),
    .sel(1'b1), .clk(CLK), .ld(clu_1_lw), .clr(1'b0));

  // Notes on the sheet:
  //   dest
  //   op
  //   SW
  //   R/I
  //   LW
  //   src1
  //   src2
  //   src2
  //   dest
  //   src1
  //   immed data
  //   immed select
endmodule

module Program_Counter (
  input  CLK,
  input  Reset,
  output [7:0] out_3
);

  wire [7:0] adder_1_out, bit_extender_1_out;

  assign bit_extender_1_out = {{7{1'b0}}, 1'b1};  // Bit_Extender bit_extender_1
  Adder adder_1 (.a(out_3), .b(bit_extender_1_out), .out(adder_1_out));  // open: cin, cout
  Register register_1 (.D(adder_1_out), .en(1'b1), .Q(out_3), .clk(CLK), .clr(Reset));
endmodule

module Full_CPU (
  input  Reset,
  input  CLK,
  output [3:0] CPU_Op_Out
);

  wire clu_1_lw, clu_1_r_i, clu_1_sw, multiplexer_1_out;
  wire [1:0] clu_1_alu_op;
  wire [2:0] multiplexer_2_out;
  wire [3:0] bit_extender_1_out, multiplexer_3_out, multiplexer_4_out, n8x4_bit_register_file_1_read_1_data,
       n8x4_bit_register_file_1_read_2_data, ram_2_data;
  wire [7:0] program_counter_1_out_3;
  wire [13:0] ram_1_data;

  Program_Counter program_counter_1 (.CLK(CLK), .Reset(Reset), .out_3(program_counter_1_out_3));
  // Probe on program_counter_1_out_3
  // Probe on ram_1_data
  RAM #(.dataWidth(14)) ram_1 (.addr(program_counter_1_out_3), .data(ram_1_data));  // open: sel, clk, ld, clr
  CLU clu_1 (.Opcode(ram_1_data[13:9]), .ALU_op(clu_1_alu_op), .LW(clu_1_lw), .SW(clu_1_sw), .R_I(clu_1_r_i));
  Multiplexer multiplexer_1 (.in0(1'b1), .in1(1'b0), .out(multiplexer_1_out), .sel(clu_1_sw));  // open: en
  Multiplexer #(.width(3)) multiplexer_2 (
    .in0(ram_1_data[2:0]), .in1(ram_1_data[8:6]), .out(multiplexer_2_out), .sel(clu_1_sw));  // open: en
  _8x4_bit_Register_File u_8x4_bit_register_file_1 (
    .Read_Addr_2(multiplexer_2_out), .Data_In(multiplexer_4_out),
    .Read_1_Data(n8x4_bit_register_file_1_read_1_data), .Read_Addr_1(ram_1_data[5:3]),
    .Write_Enable(multiplexer_1_out), .Write_Addr(ram_1_data[8:6]),
    .Read_2_Data(n8x4_bit_register_file_1_read_2_data), .Clock(CLK));
  assign bit_extender_1_out = {{1{ram_1_data[2]}}, ram_1_data[2:0]};  // Bit_Extender bit_extender_1
  Multiplexer #(.width(4), .enable("false")) multiplexer_3 (
    .in0(n8x4_bit_register_file_1_read_2_data), .in1(bit_extender_1_out), .out(multiplexer_3_out),
    .sel(clu_1_r_i));
  Multiplexer #(.width(4)) multiplexer_4 (
    .in0(CPU_Op_Out), .in1(ram_2_data), .out(multiplexer_4_out), .sel(clu_1_lw));  // open: en
  _4_bit_ALU u_4_bit_alu_1 (
    .A(n8x4_bit_register_file_1_read_1_data), .ALU_Out(CPU_Op_Out), .B(multiplexer_3_out),
    .ALU_Op(clu_1_alu_op));
  RAM #(.addrWidth(4), .dataWidth(4), .bus("separate")) ram_2 (
    .addr(CPU_Op_Out), .din(n8x4_bit_register_file_1_read_2_data), .data(ram_2_data), .str(clu_1_sw),
    .sel(1'b1), .clk(CLK), .ld(clu_1_lw), .clr(1'b0));

  // Notes on the sheet:
  //   src2
  //   dest
  //   src1
  //   immed data
  //   immed select
endmodule
